# Fritzing sketch RFID (saved by Fritzing 0.9.10b)
breadboards: 1

parts:
  Mod1 = Amica NodeMCU DEVKIT 1.0
  Part1 = RFID-RC522-v2
  Mod2 = KY-009 Full Color RGB LED SMD Module [package="Breakout board"]

nets:
  N1: Mod1.pin1, Mod1.pin_10
  N2: Mod1.pin2, Mod1.pin_9, Mod1.pin_25, Part1.RST, Mod2.-
  N3: Mod1.pin6, Part1.MOSI
  N4: Mod1.pin7, Part1.MISO
  N5: Mod1.pin8, Part1.SCK
  N6: Mod1.pin_11, Mod2.R
  N7: Mod1.pin_13, Part1.GND
  N8: Mod1.pin_14, Part1.SDA
  N9: Mod1.pin_15, Mod2.G
  N10: Mod1.pin_18, Part1.3_3V

notes:
  Device requires 5V availiable on the VV pin on my boads

custom parts:
  RFID-RC522-v2: A simple China made RFID-RC522 Reader; do check the pin labels, as this is a MFRC522 based clone.
  KY-009 Full Color RGB LED SMD Module: KY-009 RGB full color LED Module, emits a range of colors by mixing red, green and blue light. The amount of each color is adjusted using PWM.
